# Fritzing sketch Schaltung1 (saved by Fritzing 0.9.3b)
breadboards: 1

parts:
  LED1 = LED - 5mm [color="Red (633nm)" package="5 mm [THT]"]
  LED2 = LED - 5mm [color="Red (633nm)" package="5 mm [THT]"]
  LED3 = LED - 5mm [color="White (8000K)" package="5 mm [THT]"]
  LED4 = LED - 5mm [color="White (8000K)" package="5 mm [THT]"]
  LED5 = LED - 5mm [color="Orange (605nm)" package="5 mm [THT]"]
  LED6 = LED - 5mm [color="Orange (605nm)" package="5 mm [THT]"]
  J1 = Piezo Speaker
  Bauteil1 = Arduino Nano (Rev3.0) (ICSP)
  M1 = DC Motor
  BAT1 = BC9VPC [package=bc9vpc]
  Q1 = Basic FET N-Channel [package="D2Pak [SMD]"]
  R6 = Resistor [tolerance=±5% resistance=220 package="1206 [SMD]"]
  M2 = DC Motor
  J2 = Basic Servo
  R5 = Resistor [tolerance=±5% resistance=220 package="1206 [SMD]"]
  R3 = Resistor [tolerance=±5% resistance=220 package="1206 [SMD]"]
  R1 = Resistor [tolerance=±5% resistance=220 package="1206 [SMD]"]
  R2 = Resistor [tolerance=±5% resistance=220 package="1206 [SMD]"]
  Q2 = NPN-Transistor [package="SOT-23 [SMD]"]
  Q5 = NPN-Transistor [package="SOT-23 [SMD]"]
  Q6 = NPN-Transistor [package="SOT-23 [SMD]"]
  Q7 = NPN-Transistor [package="SOT-23 [SMD]"]

nets:
  N1: LED1.cathode, R1.Pin_0
  N2: LED1.anode, LED2.cathode
  N3: LED2.anode, Q5.2
  N4: LED3.cathode, R2.Pin_0
  N5: LED3.anode, LED4.cathode
  N6: LED4.anode, J1.pin1, Bauteil1.GND, Bauteil1.D2, Bauteil1.RESET, BAT1.V-, Q1.source, R2.Pin_1, Q2.2, Q2.1, Q5.0, Q5.1, Q6.1, Q7.1
  N7: LED5.cathode, LED6.cathode, R3.Pin_0
  N8: LED5.anode, Q7.2
  N9: LED6.anode, Q6.2
  N10: J1.pin2, Bauteil1.D12/MISO
  N11: Bauteil1.D3, Q2.0
  N12: Bauteil1.D4, Q6.0
  N13: Bauteil1.D5, J2.pulse
  N14: Bauteil1.D6, Q1.Gate
  N15: Bauteil1.D7, Q7.0
  VIN: Bauteil1.VIN, M1.pin_2, BAT1.V+, M2.pin_2, J2.vcc
  N16: Bauteil1.5V, R3.Pin_1, R1.Pin_1
  N17: M1.pin_1, R6.Pin_0, M2.pin_1
  N18: Q1.drain, R6.Pin_1
  N19: J2.gnd, R5.Pin_0

notes:
  LEDs bei 20mA:
  R1 = bei 1,8V -> 35R
  R2 = bei 3,5V -> 20R
  R3 = bei 2,2V -> 52,5R
  Motoren:
  R5 =
  R6 =
